# Fritzing sketch innovatek-Lora (saved by Fritzing 1.0.4)

parts:
  A1 = NEO-6M GPS Module [part_number=GY-GPS6MV2]
  U2 = LIPO-1000mAh [package=lipo-1000]
  S1 = Pushbutton [package="[THT]"]
  A2 = SM5308 battery charger module
  M1 = DOIT Esp32 DevKit v1 (30 pins long, 11 pins width) [part_number=ESP32S-PIN30]
  SIM800L1 = SIM800L
  MIC1 = Microphone
  U3 = LM2596 step down module
  LED2 = smd LED [color="Blue (470nm)" package="1206 [SMD]"]
  LED3 = smd LED [color="Green (560nm)" package="0805 [SMD]"]
  LED4 = smd LED [color="Orange (612nm)" package="0805 [SMD]"]
  S3 = Pushbutton [package="[THT]"]
  S4 = Pushbutton [package="[THT]"]
  R4 = Resistor [tolerance=±5% resistance=220 package="1206 [SMD]"]
  R5 = Resistor [tolerance=±5% resistance=220 package="1206 [SMD]"]
  R6 = Resistor [tolerance=±5% resistance=220 package="1206 [SMD]"]
  LoRa_Module1 = Ra-01 - LoRa Module SX1278 [part_number=SX1278]

nets:
  GND: A1.GND, S1.Pin_3, M1.GND, LED2.cathode, LED3.cathode, LED4.cathode, S3.Pin_3, S3.Pin_4, LoRa_Module1.GND
  N1: A1.Tx, M1.RX2
  N2: A1.Rx, M1.TX2
  VCC: A1.Vcc, M1.3V3, LoRa_Module1.3.3V
  N3: U2.+, A2.Pin_2
  N4: U2.-, A2.Pin_1, A2.Pin_5, SIM800L1.GND, U3.IN-, U3.OUT-, S4.Pin_4
  N5: S1.Pin_1, S1.Pin_2, M1.D4
  N6: A2.Pin_3, S4.Pin_2
  N7: A2.Pin_4, M1.VIN, U3.IN+
  N8: M1.D15, LoRa_Module1.NSS
  N9: M1.D5, S3.Pin_1, S3.Pin_2
  N10: M1.D18, LoRa_Module1.SCK
  N11: M1.RX0, SIM800L1.TXD
  N12: M1.TX0, SIM800L1.RXD
  N13: M1.D22, LoRa_Module1.MISO
  N14: M1.D23, LoRa_Module1.MOSI
  N15: M1.D33, LoRa_Module1.DIO0
  N16: M1.D14, R6.Pin_0
  N17: M1.D12, R5.Pin_0
  N18: M1.D13, R4.Pin_0
  N19: SIM800L1.VCC, U3.OUT+
  N20: SIM800L1.MCP, MIC1.pin2
  N21: SIM800L1.MCN, MIC1.pin1
  N22: LED2.anode, R4.Pin_1
  N23: LED3.anode, R5.Pin_1
  N24: LED4.anode, R6.Pin_1

notes:
  GorilaTrack
  4V 2A
  Innovatek proyecto
  EncendidoESP32
  //Presionar 3s - Off
  Boton Emergencia
  //Presionar 4s -Cancel
  Encendido Fuente
  //2 Pulsasiones- Off

custom parts:
  NEO-6M GPS Module: GY-GPS6MV2 NEO-6M GPS Module Module based on U-blox NEO-6M GPS engine, incorporating regulator for 3.3-5V DC input, MS621FE-compatible rechargeable battery for backup and EEPROM for storing configuration settings. Links: NEO-6 series product information page NEO-6 Datasheet
  SM5308 battery charger module: Charger module for Lipo Battery from Usb, 5v 2a, Sm5308 chip.
  DOIT Esp32 DevKit v1 (30 pins long, 11 pins width): The DOIT Esp32 DevKit v1 is one of the development board created by DOIT to evaluate the ESP-WROOM-32 module. It is based on the ESP32 microcontroller that boasts Wifi, Bluetooth, Ethernet and Low Power support all in a single chip. (vanepp) made breadboard work, adjusted pin numbering and labels and reduced size of schematic and cleaned up pcb. This chip is 30pins long (2 x15) and 11 pins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
  SIM800L: SIM800L is a miniature cellular module which allows for GPRS transmission, sending and receiving SMS and making and receiving voice calls. Low cost and small footprint and quad band frequency support make this module perfect solution for any project that require long range connectivity. After connecting power module boots up, searches for cellular network and login automatically. On board LED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
  LM2596 step down module: LM2596 DC-DC step down power supply module 3 A.
  Ra-01 - LoRa Module SX1278: The Ra-01 LoRa Module featuring the SX1278 engine by Semtech. Module by AI-Thinker. Module (Ra-01) specifications from: https://www.banggood.com/Ra-01-Smart-Electronics-SX1278-LoRa-Spread-Spectrum-Wireless-Module-Ultra-Far-10KM-433M-p-1130769.html Description: Power supply: DC1.8-3.7V(3.3V) Chip: SX1278 Frequency: 433Mhz Operating temperature: -40~+85°C On Sheild Description (may vary by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
